# Fritzing sketch traffic (saved by Fritzing 0.9.1b)
breadboards: 1

parts:
  Part1 = Spark Core (v1.0)
  IC1 = IC, DIP package, 18 pins [chip_label=ULN2803A]
  R1 = Resistor [tolerance=±5% resistance=1k package=THT]
  D1 = Zener Diode [part_number=1N4732A breakdown_voltage=3.6V package="Melf DO-213 AB [SMD]"]
  R2 = Resistor [tolerance=±5% resistance=1k package=THT]
  R3 = Resistor [tolerance=±5% resistance=1k package=THT]
  D2 = Zener Diode [part_number=1N4732A breakdown_voltage=3.6V package="Melf DO-213 AB [SMD]"]
  D3 = Zener Diode [part_number=1N4732A breakdown_voltage=3.6V package="Melf DO-213 AB [SMD]"]
  C1 = Ceramic Capacitor [capacitance=1µF package="100 mil [THT, multilayer]"]
  U1 = Voltage Regulator - 5V [package="TO220 [THT]"]
  C2 = Electrolytic Capacitor [capacitance=47µF voltage=20V package="100 mil [THT, electrolytic]"]
  C3 = Electrolytic Capacitor [capacitance=0.1mF package="100 mil [THT, electrolytic]"]
  Power_plug1 = Power plug
  R4 = Resistor [tolerance=±5% resistance=1k package=THT]
  R5 = Resistor [tolerance=±5% resistance=1k package=THT]
  R6 = Resistor [tolerance=±5% resistance=1k package=THT]
  LED1 = LED - 5mm [color="Red (633nm)" package="5 mm [THT]"]
  LED2 = LED - 5mm [color="Yellow (574nm)" package="5 mm [THT]"]
  LED3 = LED - 5mm [color="Green (555nm)" package="5 mm [THT]"]

nets:
  GND: Part1.GND, IC1.pin9, D1.anode, D2.anode, D3.anode, C1.1, U1.GND, C2.-, C3.-, Power_plug1.GND
  N1: Part1.VIN, C1.0, U1.output_voltage, C3.+
  N2: Part1.D2, R3.Pin_1, D3.cathode
  N3: Part1.D4, R2.Pin_1, D2.cathode
  N4: Part1.D6, R1.Pin_1, D1.cathode
  N5: IC1.pin4, R3.Pin_0
  N6: IC1.pin6, R2.Pin_0
  N7: IC1.pin8, R1.Pin_0
  N8: IC1.pin10, Power_plug1.VCC, LED1.anode, LED2.anode, LED3.anode
  N9: IC1.pin11, R6.Pin_0
  N10: IC1.pin13, R5.Pin_0
  N11: IC1.pin15, R4.Pin_0
  N12: U1.input_voltage, C2.+
  N13: R4.Pin_1, LED1.cathode
  N14: R5.Pin_1, LED2.cathode
  N15: R6.Pin_1, LED3.cathode
